# Fritzing sketch Project_Schematic (saved by Fritzing 0.9.3b)
breadboards: 2

parts:
  Part1 = Arduino Nano 33 IOT
  OLED_I2C1 = OLED 128x64 I2C Monochrome Display
  DHT1 = DHT22 Humidity and Temperature Sensor
  Part2 = Barometric Pressure Sensor - BMP180 Breakout (GY-68)  # not connected
  YL-83_-_Control_Board1 = YL-83 Rain Sensor - Control Board
  YL-83_-_Detection_Board1 = YL-83 Rain Sensor - Detection Board  # not connected
  M1 = bn-220- GPS-module

nets:
  N1: Part1.RESET, Part1.A7
  GND: Part1.GND, Part1.D13~, OLED_I2C1.GND, DHT1.NULL, YL-83_-_Control_Board1.GND, M1.pin_1, M1.pin_2
  N2: Part1.D11/MOSI, Part1.+5V
  N3: Part1.A5, OLED_I2C1.SCK
  N4: Part1.A4, OLED_I2C1.SDA
  3V3: Part1.3V3, OLED_I2C1.VDD, YL-83_-_Control_Board1.VCC, M1.pin_3, M1.pin_4

notes:
  Please note: DHT22 has 3 pins, starting from Left to right:
  P1: Vcc
  P2: V_out
  P3: GND

custom parts:
  Arduino Nano 33 IOT: The Arduino Nano 33 IoT is the easiest and cheapest point of entry to enhance existing devices (and creating new ones) to be part of the IoT and designing pico-network applications. Whether you are looking at building a sensor network connected to your office or home router, or if you want to create a BLE device sending data to a cellphone, the Nano 33 IoT is your one-stop-solution for many of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
  YL-83 Rain Sensor - Control Board: The YL-83 is a rain sensor that has more resistance when dry and less resistance when wet. The module runs at 5V.
  YL-83 Rain Sensor - Detection Board: The YL-83 is a rain sensor that has more resistance when dry and less resistance when wet. The module runs at 5V.
  bn-220- GPS-module: bn-220l GPS module. Chipset : 8030-KT Receiving Format : GPS,GLONASS,Galileo,BeiDou,QZSS and SBAS
